// Logisim project cpu.circ as structural Verilog: 1 circuit, main circuit cpu
module cpu (
  input  clk,
  input  [31:0] INSTRUCTION,
  input  [31:0] READ_DATA,
  output [31:0] WRITE_ADDRESS,
  output [31:0] PROGRAM_COUNTER,
  output [31:0] ra,
  output [31:0] sp,
  output [31:0] t0,
  output [31:0] t1,
  output [31:0] t2,
  output [31:0] s0,
  output [31:0] s1,
  output [31:0] a0,
  output [31:0] tohost,
  output [3:0] WRITE_ENABLE,
  output [31:0] WRITE_DATA
);

  wire [31:0] adder_1_out, imm, INSTRUCTIONID, RD1, RD2, RESULT, WD;

  Adder #(.width(32)) adder_1 (.a(PROGRAM_COUNTER), .b(32'h4), .out(adder_1_out));  // open: cin, cout
  Register #(.width(32)) PC (.D(adder_1_out), .en(1'b1), .clk(clk), .Q(PROGRAM_COUNTER));  // open: clr
  Register #(.width(32)) register_1 (.D(INSTRUCTION), .en(1'b1), .clk(clk), .Q(INSTRUCTIONID));  // open: clr
  imm_gen imm_gen_1 (.inst(INSTRUCTIONID), .imm(imm));  // open: ImmSel
  // control_logic control_logic_1: pin names not known
  regfile regfile_1 (
    .rs1(INSTRUCTIONID[19:15]), .rs2(INSTRUCTIONID[24:20]), .rd(INSTRUCTIONID[11:7]), .Write_Data(WD),
    .RegWEn(1'b1), .clk(clk), .ra(ra), .sp(sp), .t0(t0), .t1(t1), .t2(t2), .s0(s0), .s1(s1), .a0(a0),
    .Read_Data_1(RD1), .Read_Data_2(RD2));
  // branch_comp branch_comp_1: pin names not known
  // csr csr_1: pin names not known; wires that end beside it: tohost
  alu alu_1 (.Result(RESULT), .A(RD1), .B(imm), .ALUSel(4'b0000));
  Multiplexer #(.enable("false"), .width(32)) multiplexer_1 (.in0(RESULT), .in1(READ_DATA), .out(WD), .sel(1'b0));

  // Other names for the same wires on the sheet: rd[4:0] = INSTRUCTIONID[11:7]; rs1[4:0] = INSTRUCTIONID[19:15];
  //   rs2[4:0] = INSTRUCTIONID[24:20]

  // Notes on the sheet:
  //   Output to IMEM
  //   IMEM (do **NOT** move this)
  //   Inputs from IMEM
  //   It is OK to move the PC, RegFile, ALU, MEM, Branch Comp, Imm Gen, and Control Logic to wherever is most convenient for you when constructing your CPU, and to delete this text
  //   Inputs/Outputs for testing. Do **NOT** move these.
  //   Outputs To DMEM
  //   DMEM (do **NOT** move this)
  //   Inputs From DMEM
endmodule
