// Logisim project regfile.circ as structural Verilog: 2 circuits, main circuit regfile
module regfile (
  input  [4:0] rs1,
  input  [4:0] rs2,
  input  [4:0] rd,
  input  [31:0] Write_Data,
  input  RegWEn,
  input  clk,
  output [31:0] ra,
  output [31:0] sp,
  output [31:0] t0,
  output [31:0] t1,
  output [31:0] t2,
  output [31:0] s0,
  output [31:0] s1,
  output [31:0] a0,
  output [31:0] Read_Data_1,
  output [31:0] Read_Data_2
);

  wire demultiplexer_2_out0, write_en1, write_en2, write_en3, write_en4, write_en5, write_en6, write_en7,
       write_en8, write_en9, write_en10, write_en11, write_en12, write_en13, write_en14, write_en15,
       write_en16, write_en17, write_en18, write_en19, write_en20, write_en21, write_en22, write_en23,
       write_en24, write_en25, write_en26, write_en27, write_en28, write_en29, write_en30, write_en31;
  wire [31:0] wD0, wD1, wD2, wD3, wD4, wD5, wD6, wD7, wD8, wD9, wD10, wD11, wD12, wD13, wD14, wD15, wD16,
       wD17, wD18, wD19, wD20, wD21, wD22, wD23, wD24, wD25, wD26, wD27, wD28, wD29, wD30, wD31, x0, x3, x4,
       x11, x12, x13, x14, x15, x16, x17, x18, x19, x20, x21, x22, x23, x24, x25, x26, x27, x28, x29, x30,
       x31;

  Demultiplexer #(.enable("false"), .select(5), .width(32)) demultiplexer_1 (
    .out0(wD0), .out1(wD1), .out2(wD2), .out3(wD3), .out4(wD4), .out5(wD5), .out6(wD6), .out7(wD7),
    .out8(wD8), .out9(wD9), .out10(wD10), .out11(wD11), .out12(wD12), .out13(wD13), .out14(wD14),
    .out15(wD15), .out16(wD16), .out17(wD17), .out18(wD18), .out19(wD19), .out20(wD20), .out21(wD21),
    .out22(wD22), .out23(wD23), .out24(wD24), .out25(wD25), .out26(wD26), .out27(wD27), .out28(wD28),
    .out29(wD29), .out30(wD30), .out31(wD31), .in(Write_Data), .sel(rd));
  Demultiplexer #(.enable("false"), .select(5)) demultiplexer_2 (
    .out0(demultiplexer_2_out0), .out1(write_en1), .out2(write_en2), .out3(write_en3), .out4(write_en4),
    .out5(write_en5), .out6(write_en6), .out7(write_en7), .out8(write_en8), .out9(write_en9),
    .out10(write_en10), .out11(write_en11), .out12(write_en12), .out13(write_en13), .out14(write_en14),
    .out15(write_en15), .out16(write_en16), .out17(write_en17), .out18(write_en18), .out19(write_en19),
    .out20(write_en20), .out21(write_en21), .out22(write_en22), .out23(write_en23), .out24(write_en24),
    .out25(write_en25), .out26(write_en26), .out27(write_en27), .out28(write_en28), .out29(write_en29),
    .out30(write_en30), .out31(write_en31), .in(RegWEn), .sel(rd));
  // NoConnect on demultiplexer_2_out0
  Register #(.width(32)) register_1 (.D(wD0), .en(1'b0), .clk(clk), .Q(x0), .clr(1'b1));
  Register #(.width(32)) register_2 (.D(wD1), .en(write_en1), .clk(clk), .Q(ra));  // open: clr
  Register #(.width(32)) register_3 (.D(wD2), .en(write_en2), .clk(clk), .Q(sp));  // open: clr
  Register #(.width(32)) register_4 (.D(wD3), .en(write_en3), .clk(clk), .Q(x3));  // open: clr
  Register #(.width(32)) register_5 (.D(wD4), .en(write_en4), .clk(clk), .Q(x4));  // open: clr
  Register #(.width(32)) register_6 (.D(wD5), .en(write_en5), .clk(clk), .Q(t0));  // open: clr
  Register #(.width(32)) register_7 (.D(wD6), .en(write_en6), .clk(clk), .Q(t1));  // open: clr
  Register #(.width(32)) register_8 (.D(wD7), .en(write_en7), .clk(clk), .Q(t2));  // open: clr
  Register #(.width(32)) register_9 (.D(wD8), .en(write_en8), .clk(clk), .Q(s0));  // open: clr
  Register #(.width(32)) register_10 (.D(wD9), .en(write_en9), .clk(clk), .Q(s1));  // open: clr
  Register #(.width(32)) register_11 (.D(wD10), .en(write_en10), .clk(clk), .Q(a0));  // open: clr
  Register #(.width(32)) register_12 (.D(wD11), .en(write_en11), .clk(clk), .Q(x11));  // open: clr
  Register #(.width(32)) register_13 (.D(wD12), .en(write_en12), .clk(clk), .Q(x12));  // open: clr
  Register #(.width(32)) register_14 (.D(wD13), .en(write_en13), .clk(clk), .Q(x13));  // open: clr
  Register #(.width(32)) register_15 (.D(wD14), .en(write_en14), .clk(clk), .Q(x14));  // open: clr
  Register #(.width(32)) register_16 (.D(wD15), .en(write_en15), .clk(clk), .Q(x15));  // open: clr
  Register #(.width(32)) register_17 (.D(wD16), .en(write_en16), .clk(clk), .Q(x16));  // open: clr
  Register #(.width(32)) register_18 (.D(wD17), .en(write_en17), .clk(clk), .Q(x17));  // open: clr
  Register #(.width(32)) register_19 (.D(wD18), .en(write_en18), .clk(clk), .Q(x18));  // open: clr
  Register #(.width(32)) register_20 (.D(wD19), .en(write_en19), .clk(clk), .Q(x19));  // open: clr
  Register #(.width(32)) register_21 (.D(wD20), .en(write_en20), .clk(clk), .Q(x20));  // open: clr
  Register #(.width(32)) register_22 (.D(wD21), .en(write_en21), .clk(clk), .Q(x21));  // open: clr
  Register #(.width(32)) register_23 (.D(wD22), .en(write_en22), .clk(clk), .Q(x22));  // open: clr
  Register #(.width(32)) register_24 (.D(wD23), .en(write_en23), .clk(clk), .Q(x23));  // open: clr
  Register #(.width(32)) register_25 (.D(wD24), .en(write_en24), .clk(clk), .Q(x24));  // open: clr
  Register #(.width(32)) register_26 (.D(wD25), .en(write_en25), .clk(clk), .Q(x25));  // open: clr
  Register #(.width(32)) register_27 (.D(wD26), .en(write_en26), .clk(clk), .Q(x26));  // open: clr
  Register #(.width(32)) register_28 (.D(wD27), .en(write_en27), .clk(clk), .Q(x27));  // open: clr
  Register #(.width(32)) register_29 (.D(wD28), .en(write_en28), .clk(clk), .Q(x28));  // open: clr
  Register #(.width(32)) register_30 (.D(wD29), .en(write_en29), .clk(clk), .Q(x29));  // open: clr
  Register #(.width(32)) register_31 (.D(wD30), .en(write_en30), .clk(clk), .Q(x30));  // open: clr
  Register #(.width(32)) register_32 (.D(wD31), .en(write_en31), .clk(clk), .Q(x31));  // open: clr
  Multiplexer #(.enable("false"), .select(5), .width(32)) multiplexer_1 (
    .in0(x0), .in1(ra), .in2(sp), .in3(x3), .in4(x4), .in5(t0), .in6(t1), .in7(t2), .in8(s0), .in9(s1),
    .in10(a0), .in11(x11), .in12(x12), .in13(x13), .in14(x14), .in15(x15), .in16(x16), .in17(x17),
    .in18(x18), .in19(x19), .in20(x20), .in21(x21), .in22(x22), .in23(x23), .in24(x24), .in25(x25),
    .in26(x26), .in27(x27), .in28(x28), .in29(x29), .in30(x30), .in31(x31), .out(Read_Data_1), .sel(rs1));
  Multiplexer #(.enable("false"), .select(5), .width(32)) multiplexer_2 (
    .in0(x0), .in1(ra), .in2(sp), .in3(x3), .in4(x4), .in5(t0), .in6(t1), .in7(t2), .in8(s0), .in9(s1),
    .in10(a0), .in11(x11), .in12(x12), .in13(x13), .in14(x14), .in15(x15), .in16(x16), .in17(x17),
    .in18(x18), .in19(x19), .in20(x20), .in21(x21), .in22(x22), .in23(x23), .in24(x24), .in25(x25),
    .in26(x26), .in27(x27), .in28(x28), .in29(x29), .in30(x30), .in31(x31), .out(Read_Data_2), .sel(rs2));

  // Other names for the same wires on the sheet: read_data1[31:0] = Read_Data_1; read_data2[31:0] = Read_Data_2;
  //   read_reg1[4:0] = rs1; read_reg2[4:0] = rs2; write_en = RegWEn; write_reg[4:0] = rd

  // Notes on the sheet:
  //   INPUTS to your circuit
  //   DON'T CHANGE THE LOCATIONS OF THE INPUTS AND OUTPUTS!
  //   These are DEBUG/TEST outputs from your circuit.
  //   OUTPUTS from your circuit
endmodule

module regfileHelper (
  input  [31:0] write_data,
  input  [4:0] wirte_reg,
  input  [4:0] read_reg1,
  input  reg_writen,
  input  [4:0] read_reg2,
  input  clk,
  output [31:0] read_data1,
  output [31:0] read_data2
);

  wire demultiplexer_2_out0, write_en1, write_en2, write_en3, write_en4, write_en5, write_en6, write_en7,
       write_en8, write_en9, write_en10, write_en11, write_en12, write_en13, write_en14, write_en15,
       write_en16, write_en17, write_en18, write_en19, write_en20, write_en21, write_en22, write_en23,
       write_en24, write_en25, write_en26, write_en27, write_en28, write_en29, write_en30, write_en31;
  wire [31:0] a0, ra, s0, s1, sp, t0, t1, t2, wD0, wD1, wD2, wD3, wD4, wD5, wD6, wD7, wD8, wD9, wD10, wD11,
       wD12, wD13, wD14, wD15, wD16, wD17, wD18, wD19, wD20, wD21, wD22, wD23, wD24, wD25, wD26, wD27, wD28,
       wD29, wD30, wD31, x0, x3, x4, x11, x12, x13, x14, x15, x16, x17, x18, x19, x20, x21, x22, x23, x24,
       x25, x26, x27, x28, x29, x30, x31;

  Demultiplexer #(.enable("false"), .select(5), .width(32)) demultiplexer_1 (
    .out0(wD0), .out1(wD1), .out2(wD2), .out3(wD3), .out4(wD4), .out5(wD5), .out6(wD6), .out7(wD7),
    .out8(wD8), .out9(wD9), .out10(wD10), .out11(wD11), .out12(wD12), .out13(wD13), .out14(wD14),
    .out15(wD15), .out16(wD16), .out17(wD17), .out18(wD18), .out19(wD19), .out20(wD20), .out21(wD21),
    .out22(wD22), .out23(wD23), .out24(wD24), .out25(wD25), .out26(wD26), .out27(wD27), .out28(wD28),
    .out29(wD29), .out30(wD30), .out31(wD31), .in(write_data), .sel(wirte_reg));
  Demultiplexer #(.enable("false"), .select(5)) demultiplexer_2 (
    .out0(demultiplexer_2_out0), .out1(write_en1), .out2(write_en2), .out3(write_en3), .out4(write_en4),
    .out5(write_en5), .out6(write_en6), .out7(write_en7), .out8(write_en8), .out9(write_en9),
    .out10(write_en10), .out11(write_en11), .out12(write_en12), .out13(write_en13), .out14(write_en14),
    .out15(write_en15), .out16(write_en16), .out17(write_en17), .out18(write_en18), .out19(write_en19),
    .out20(write_en20), .out21(write_en21), .out22(write_en22), .out23(write_en23), .out24(write_en24),
    .out25(write_en25), .out26(write_en26), .out27(write_en27), .out28(write_en28), .out29(write_en29),
    .out30(write_en30), .out31(write_en31), .in(reg_writen), .sel(wirte_reg));
  // NoConnect on demultiplexer_2_out0
  Register #(.width(32)) register_1 (.D(wD0), .en(1'b0), .clk(clk), .Q(x0), .clr(1'b1));
  Register #(.width(32)) register_2 (.D(wD1), .en(write_en1), .clk(clk), .Q(ra));  // open: clr
  Register #(.width(32)) register_3 (.D(wD2), .en(write_en2), .clk(clk), .Q(sp));  // open: clr
  Register #(.width(32)) register_4 (.D(wD3), .en(write_en3), .clk(clk), .Q(x3));  // open: clr
  Register #(.width(32)) register_5 (.D(wD4), .en(write_en4), .clk(clk), .Q(x4));  // open: clr
  Register #(.width(32)) register_6 (.D(wD5), .en(write_en5), .clk(clk), .Q(t0));  // open: clr
  Register #(.width(32)) register_7 (.D(wD6), .en(write_en6), .clk(clk), .Q(t1));  // open: clr
  Register #(.width(32)) register_8 (.D(wD7), .en(write_en7), .clk(clk), .Q(t2));  // open: clr
  Register #(.width(32)) register_9 (.D(wD8), .en(write_en8), .clk(clk), .Q(s0));  // open: clr
  Register #(.width(32)) register_10 (.D(wD9), .en(write_en9), .clk(clk), .Q(s1));  // open: clr
  Register #(.width(32)) register_11 (.D(wD10), .en(write_en10), .clk(clk), .Q(a0));  // open: clr
  Register #(.width(32)) register_12 (.D(wD11), .en(write_en11), .clk(clk), .Q(x11));  // open: clr
  Register #(.width(32)) register_13 (.D(wD12), .en(write_en12), .clk(clk), .Q(x12));  // open: clr
  Register #(.width(32)) register_14 (.D(wD13), .en(write_en13), .clk(clk), .Q(x13));  // open: clr
  Register #(.width(32)) register_15 (.D(wD14), .en(write_en14), .clk(clk), .Q(x14));  // open: clr
  Register #(.width(32)) register_16 (.D(wD15), .en(write_en15), .clk(clk), .Q(x15));  // open: clr
  Register #(.width(32)) register_17 (.D(wD16), .en(write_en16), .clk(clk), .Q(x16));  // open: clr
  Register #(.width(32)) register_18 (.D(wD17), .en(write_en17), .clk(clk), .Q(x17));  // open: clr
  Register #(.width(32)) register_19 (.D(wD18), .en(write_en18), .clk(clk), .Q(x18));  // open: clr
  Register #(.width(32)) register_20 (.D(wD19), .en(write_en19), .clk(clk), .Q(x19));  // open: clr
  Register #(.width(32)) register_21 (.D(wD20), .en(write_en20), .clk(clk), .Q(x20));  // open: clr
  Register #(.width(32)) register_22 (.D(wD21), .en(write_en21), .clk(clk), .Q(x21));  // open: clr
  Register #(.width(32)) register_23 (.D(wD22), .en(write_en22), .clk(clk), .Q(x22));  // open: clr
  Register #(.width(32)) register_24 (.D(wD23), .en(write_en23), .clk(clk), .Q(x23));  // open: clr
  Register #(.width(32)) register_25 (.D(wD24), .en(write_en24), .clk(clk), .Q(x24));  // open: clr
  Register #(.width(32)) register_26 (.D(wD25), .en(write_en25), .clk(clk), .Q(x25));  // open: clr
  Register #(.width(32)) register_27 (.D(wD26), .en(write_en26), .clk(clk), .Q(x26));  // open: clr
  Register #(.width(32)) register_28 (.D(wD27), .en(write_en27), .clk(clk), .Q(x27));  // open: clr
  Register #(.width(32)) register_29 (.D(wD28), .en(write_en28), .clk(clk), .Q(x28));  // open: clr
  Register #(.width(32)) register_30 (.D(wD29), .en(write_en29), .clk(clk), .Q(x29));  // open: clr
  Register #(.width(32)) register_31 (.D(wD30), .en(write_en30), .clk(clk), .Q(x30));  // open: clr
  Register #(.width(32)) register_32 (.D(wD31), .en(write_en31), .clk(clk), .Q(x31));  // open: clr
  Multiplexer #(.enable("false"), .select(5), .width(32)) multiplexer_1 (
    .in0(x0), .in1(ra), .in2(sp), .in3(x3), .in4(x4), .in5(t0), .in6(t1), .in7(t2), .in8(s0), .in9(s1),
    .in10(a0), .in11(x11), .in12(x12), .in13(x13), .in14(x14), .in15(x15), .in16(x16), .in17(x17),
    .in18(x18), .in19(x19), .in20(x20), .in21(x21), .in22(x22), .in23(x23), .in24(x24), .in25(x25),
    .in26(x26), .in27(x27), .in28(x28), .in29(x29), .in30(x30), .in31(x31), .out(read_data1), .sel(read_reg1));
  Multiplexer #(.enable("false"), .select(5), .width(32)) multiplexer_2 (
    .in0(x0), .in1(ra), .in2(sp), .in3(x3), .in4(x4), .in5(t0), .in6(t1), .in7(t2), .in8(s0), .in9(s1),
    .in10(a0), .in11(x11), .in12(x12), .in13(x13), .in14(x14), .in15(x15), .in16(x16), .in17(x17),
    .in18(x18), .in19(x19), .in20(x20), .in21(x21), .in22(x22), .in23(x23), .in24(x24), .in25(x25),
    .in26(x26), .in27(x27), .in28(x28), .in29(x29), .in30(x30), .in31(x31), .out(read_data2), .sel(read_reg2));
endmodule
